// Digital circuit fourbitfulladder.dig as structural Verilog
module fourbitfulladder (
  input  Operacion,
  input  b_0,
  input  b_1,
  input  b_2,
  input  b_3,
  input  a_1,
  input  a_2,
  input  a_0,
  input  a_3,
  output c_out,
  output s_3,
  output s_2,
  output s_1,
  output s_0,
  output _2_complement
);

  wire fulladder_1_p4, fulladder_2_p4, fulladder_3_p4, not_1_out, xor_1_out, xor_2_out, xor_3_out, xor_4_out;

  xor xor_1 (xor_1_out, b_3, Operacion);
  xor xor_2 (xor_2_out, b_2, Operacion);
  xor xor_3 (xor_3_out, b_1, Operacion);
  xor xor_4 (xor_4_out, b_0, Operacion);
  // fullAdder fulladder_1: pin names not known; wires that end beside it: xor_4_out, a_0, Operacion, fulladder_1_p4, s_0
  // fullAdder fulladder_2: pin names not known; wires that end beside it: xor_3_out, a_1, fulladder_1_p4, fulladder_2_p4, s_1
  // fullAdder fulladder_3: pin names not known; wires that end beside it: xor_2_out, a_2, fulladder_2_p4, fulladder_3_p4, s_2
  // fullAdder fulladder_4: pin names not known; wires that end beside it: xor_1_out, a_3, fulladder_3_p4, c_out, s_3
  not not_1 (not_1_out, c_out);
  and and_1 (_2_complement, Operacion, not_1_out);
endmodule
